// Logisim project stack_logical_normal.circ as structural Verilog: 16 circuits, main circuit main
module main (
  input  CLK,
  input  RESET,
  input  [1:0] COMMAND,
  input  [2:0] INDEX,
  input  [3:0] IDATA,
  output [3:0] ODATA
);

  stack stack_1 (.CLK(CLK), .RESET(RESET), .COMMAND(COMMAND), .INDEX(INDEX), .IDATA(IDATA), .IO_DATA_out(ODATA));
endmodule

module stack (
  input  CLK,
  input  RESET,
  input  [1:0] COMMAND,
  input  [2:0] INDEX,
  input  [3:0] IDATA,
  output [3:0] IO_DATA_out
);

  wire and_1_out, and_2_out, counter_5_1_q_0, counter_5_1_q_1, counter_5_1_q_2, counter_5_1_q_3,
       counter_5_1_q_4, get_out, not_1_out, not_2_out, not_3_out, not_4_out, not_5_out,
       operationmanager_1_q_0, operationmanager_1_q_1, operationmanager_1_q_2, operationmanager_1_q_3,
       operationmanager_1_q_4, or_1_out, or_2_out, or_3_out, pop_out, push_out;
  wire [3:0] mem_1_odata;

  not not_1 (not_1_out, COMMAND[0]);
  not not_2 (not_2_out, COMMAND[1]);
  not not_3 (not_3_out, COMMAND[0]);
  not not_4 (not_4_out, COMMAND[1]);
  // AND_Gate nop has open pins: in0=not_1_out, in1=not_2_out, out=open
  and pop (pop_out, not_3_out, COMMAND[1]);
  and push (push_out, COMMAND[0], not_4_out);
  and get (get_out, COMMAND[0], COMMAND[1]);
  or or_1 (or_1_out, pop_out, push_out);
  not not_5 (not_5_out, pop_out);
  or or_2 (or_2_out, pop_out, get_out);
  and and_1 (and_1_out, CLK, or_1_out);
  or or_3 (or_3_out, not_5_out, push_out);
  and and_2 (and_2_out, CLK, or_2_out);
  counter_5 counter_5_1 (
    .C(and_1_out), .pop_push(or_3_out), .reset(RESET), .Q_0(counter_5_1_q_0), .Q_1(counter_5_1_q_1),
    .Q_2(counter_5_1_q_2), .Q_3(counter_5_1_q_3), .Q_4(counter_5_1_q_4));
  OperationManager operationmanager_1 (
    .pop(pop_out), .A_0(counter_5_1_q_0), .A_1(counter_5_1_q_1), .A_2(counter_5_1_q_2),
    .A_3(counter_5_1_q_3), .A_4(counter_5_1_q_4), .Push(push_out), .get(get_out), .get_0(INDEX[2]),
    .get_1(INDEX[1]), .get_2(INDEX[0]), .Q_0(operationmanager_1_q_0), .Q_1(operationmanager_1_q_1),
    .Q_2(operationmanager_1_q_2), .Q_3(operationmanager_1_q_3), .Q_4(operationmanager_1_q_4));
  MEM mem_1 (
    .A_0(operationmanager_1_q_0), .A_1(operationmanager_1_q_1), .A_2(operationmanager_1_q_2),
    .A_3(operationmanager_1_q_3), .A_4(operationmanager_1_q_4), .R_W(push_out), .CLK(CLK), .IDATA(IDATA),
    .reset(RESET), .ODATA(mem_1_odata));
  in_out_4 in_out_4_1 (.Read(and_2_out), .IDATA(mem_1_odata), .ODATA(IDATA));

  assign IO_DATA_out = IDATA;

  // Notes on the sheet:
  //   your circuit must be here
endmodule

module RS (
  input  R,
  input  C,
  input  S,
  input  reset,
  output Q,
  output not_Q
);

  wire and_1_out, and_2_out, nor_2_out;

  and and_1 (and_1_out, R, C);
  and and_2 (and_2_out, C, S);
  nor nor_1 (Q, and_1_out, not_Q);
  nor nor_2 (nor_2_out, Q, and_2_out);
  or or_1 (not_Q, nor_2_out, reset);
endmodule

module D_trigger_front (
  input  C,
  input  D,
  input  reset,
  output Q,
  output not_Q
);

  wire d_trigger_1_q, not_1_out;

  not not_1 (not_1_out, C);
  D_trigger d_trigger_1 (.C(C), .D(D), .reset(reset), .Q(d_trigger_1_q));  // open: not_Q
  D_trigger d_trigger_2 (.C(not_1_out), .D(d_trigger_1_q), .reset(reset), .Q(Q), .not_Q(not_Q));
endmodule

module counter_5 (
  input  C,
  input  pop_push,
  input  reset,
  output Q_0,
  output Q_1,
  output Q_2,
  output Q_3,
  output Q_4
);

  wire and_1_out, and_2_out, and_3_out, and_4_out, and_5_out, and_6_out, and_7_out, and_8_out, and_9_out,
       and_10_out, not_1_out, not_2_out, not_3_out, not_4_out, not_5_out, or_1_out, or_2_out, or_3_out,
       or_4_out, or_5_out, or_6_out, or_7_out;

  not not_1 (not_1_out, pop_push);
  not not_2 (not_2_out, pop_push);
  not not_3 (not_3_out, pop_push);
  not not_4 (not_4_out, pop_push);
  not not_5 (not_5_out, pop_push);
  and and_1 (and_1_out, Q_4, pop_push);
  and and_2 (and_2_out, not_1_out, Q_1);
  and and_3 (and_3_out, pop_push, Q_0);
  and and_4 (and_4_out, Q_2, not_2_out);
  and and_5 (and_5_out, Q_1, pop_push);
  and and_6 (and_6_out, Q_3, not_3_out);
  and and_7 (and_7_out, Q_2, pop_push);
  and and_8 (and_8_out, Q_4, not_4_out);
  and and_9 (and_9_out, Q_3, pop_push);
  and and_10 (and_10_out, Q_0, not_5_out);
  or or_1 (or_1_out, and_1_out, and_2_out);
  or or_2 (or_2_out, and_3_out, and_4_out);
  or or_3 (or_3_out, and_5_out, and_6_out);
  or or_4 (or_4_out, and_7_out, and_8_out);
  or or_5 (or_5_out, and_9_out, and_10_out);
  or or_6 (or_6_out, or_1_out, reset);
  or or_7 (or_7_out, C, reset);
  D_trigger_front d_trigger_front_1 (.C(C), .D(or_2_out), .reset(reset), .Q(Q_1));  // open: not_Q
  D_trigger_front d_trigger_front_2 (.C(C), .D(or_3_out), .reset(reset), .Q(Q_2));  // open: not_Q
  D_trigger_front d_trigger_front_3 (.C(C), .D(or_4_out), .reset(reset), .Q(Q_3));  // open: not_Q
  D_trigger_front d_trigger_front_4 (.C(C), .D(or_5_out), .reset(reset), .Q(Q_4));  // open: not_Q
  D_trigger_front d_trigger_front_5 (.C(or_7_out), .D(or_6_out), .reset(reset), .Q(Q_0));  // open: not_Q
endmodule

module D_trigger (
  input  C,
  input  D,
  input  reset,
  output Q,
  output not_Q
);

  wire not_1_out;

  not not_1 (not_1_out, D);
  RS rs_1 (.R(not_1_out), .C(C), .S(D), .reset(reset), .Q(Q), .not_Q(not_Q));
endmodule

module cell_4 (
  input  reset,
  input  CLK,
  input  [3:0] IDATA,
  output [3:0] ODATA
);

  D_trigger d_trigger_1 (.C(CLK), .D(IDATA[3]), .reset(reset), .Q(ODATA[3]));  // open: not_Q
  D_trigger d_trigger_2 (.C(CLK), .D(IDATA[2]), .reset(reset), .Q(ODATA[2]));  // open: not_Q
  D_trigger d_trigger_3 (.C(CLK), .D(IDATA[1]), .reset(reset), .Q(ODATA[1]));  // open: not_Q
  D_trigger d_trigger_4 (.C(CLK), .D(IDATA[0]), .reset(reset), .Q(ODATA[0]));  // open: not_Q
endmodule

module MUX (
  input  A_0,
  input  A_1,
  input  A_2,
  input  A_3,
  input  A_4,
  input  [3:0] D_0,
  input  [3:0] D_1,
  input  [3:0] D_2,
  input  [3:0] D_3,
  input  [3:0] D_4,
  output [3:0] Q
);

  wire and_1_out, and_2_out, and_3_out, and_4_out, and_5_out, and_6_out, and_7_out, and_8_out, and_9_out,
       and_10_out, and_11_out, and_12_out, and_13_out, and_14_out, and_15_out, and_16_out, and_17_out,
       and_18_out, and_19_out, and_20_out;

  and and_1 (and_1_out, A_0, D_0[3]);
  and and_2 (and_2_out, A_0, D_0[2]);
  and and_3 (and_3_out, A_0, D_0[1]);
  and and_4 (and_4_out, A_0, D_0[0]);
  and and_5 (and_5_out, A_1, D_1[3]);
  and and_6 (and_6_out, A_1, D_1[2]);
  and and_7 (and_7_out, A_1, D_1[1]);
  and and_8 (and_8_out, A_1, D_1[0]);
  and and_9 (and_9_out, A_2, D_2[3]);
  and and_10 (and_10_out, A_2, D_2[2]);
  and and_11 (and_11_out, A_2, D_2[1]);
  and and_12 (and_12_out, A_2, D_2[0]);
  and and_13 (and_13_out, A_3, D_3[3]);
  and and_14 (and_14_out, A_3, D_3[2]);
  and and_15 (and_15_out, A_3, D_3[1]);
  and and_16 (and_16_out, A_3, D_3[0]);
  and and_17 (and_17_out, A_4, D_4[3]);
  and and_18 (and_18_out, A_4, D_4[2]);
  and and_19 (and_19_out, A_4, D_4[1]);
  and and_20 (and_20_out, A_4, D_4[0]);
  or or_1 (Q[3], and_1_out, and_5_out, and_9_out, and_13_out, and_17_out);
  or or_2 (Q[2], and_2_out, and_6_out, and_10_out, and_14_out, and_18_out);
  or or_3 (Q[1], and_3_out, and_7_out, and_11_out, and_15_out, and_19_out);
  or or_4 (Q[0], and_4_out, and_8_out, and_12_out, and_16_out, and_20_out);
endmodule

module MEM (
  input  A_0,
  input  A_1,
  input  A_2,
  input  A_3,
  input  A_4,
  input  R_W,
  input  CLK,
  input  [3:0] IDATA,
  input  reset,
  output [3:0] ODATA
);

  wire and_1_out, and_2_out, and_3_out, and_4_out, and_5_out, and_6_out;
  wire [3:0] cell_4_1_odata, cell_4_2_odata, cell_4_3_odata, cell_4_4_odata, cell_4_5_odata;

  and and_1 (and_1_out, R_W, CLK);
  and and_2 (and_2_out, A_0, and_1_out);
  and and_3 (and_3_out, A_1, and_1_out);
  and and_4 (and_4_out, A_2, and_1_out);
  and and_5 (and_5_out, A_3, and_1_out);
  and and_6 (and_6_out, A_4, and_1_out);
  cell_4 cell_4_1 (.reset(reset), .CLK(and_2_out), .IDATA(IDATA), .ODATA(cell_4_1_odata));
  cell_4 cell_4_2 (.reset(reset), .CLK(and_3_out), .IDATA(IDATA), .ODATA(cell_4_2_odata));
  cell_4 cell_4_3 (.reset(reset), .CLK(and_4_out), .IDATA(IDATA), .ODATA(cell_4_3_odata));
  cell_4 cell_4_4 (.reset(reset), .CLK(and_5_out), .IDATA(IDATA), .ODATA(cell_4_4_odata));
  cell_4 cell_4_5 (.reset(reset), .CLK(and_6_out), .IDATA(IDATA), .ODATA(cell_4_5_odata));
  MUX mux_1 (
    .A_0(A_0), .A_1(A_1), .A_2(A_2), .A_3(A_3), .A_4(A_4), .D_0(cell_4_1_odata), .D_1(cell_4_2_odata),
    .D_2(cell_4_3_odata), .D_3(cell_4_4_odata), .D_4(cell_4_5_odata), .Q(ODATA));
endmodule

module OperationManager (
  input  pop,
  input  A_0,
  input  A_1,
  input  A_2,
  input  A_3,
  input  A_4,
  input  Push,
  input  get,
  input  get_0,
  input  get_1,
  input  get_2,
  output Q_0,
  output Q_1,
  output Q_2,
  output Q_3,
  output Q_4
);

  wire and_1_out, and_2_out, and_3_out, and_4_out, and_5_out, and_6_out, get0_out, get1_out, get2_out,
       get3_out, get5_out, get6_out, get7_out, minus1_or_0_1_q_0, minus1_or_0_1_q_1, minus1_or_0_1_q_2,
       minus1_or_0_1_q_3, minus1_or_0_1_q_4, minus1_or_0_2_q_0, minus1_or_0_2_q_1, minus1_or_0_2_q_2,
       minus1_or_0_2_q_3, minus1_or_0_2_q_4, minus2_or_0_1_q_0, minus2_or_0_1_q_1, minus2_or_0_1_q_2,
       minus2_or_0_1_q_3, minus2_or_0_1_q_4, minus3_or_0_1_q_0, minus3_or_0_1_q_1, minus3_or_0_1_q_2,
       minus3_or_0_1_q_3, minus3_or_0_1_q_4, minus4_or_0_1_q_0, minus4_or_0_1_q_1, minus4_or_0_1_q_2,
       minus4_or_0_1_q_3, minus4_or_0_1_q_4, not_1_out, not_2_out, not_3_out, not_4_out, not_5_out,
       not_6_out, not_7_out, not_8_out, not_9_out, not_10_out, not_11_out, not_12_out, or_1_out, or_2_out,
       or_3_out, or_4_out;

  not not_1 (not_1_out, get_1);
  not not_2 (not_2_out, get_2);
  and and_1 (and_1_out, get, get_0, not_1_out, not_2_out);
  or or_1 (or_1_out, Push, and_1_out);
  and and_2 (and_2_out, A_0, or_1_out);
  and and_3 (and_3_out, A_1, or_1_out);
  and and_4 (and_4_out, A_2, or_1_out);
  and and_5 (and_5_out, A_3, or_1_out);
  and and_6 (and_6_out, A_4, or_1_out);
  Minus1_or_0 minus1_or_0_1 (
    .A_0(A_0), .A_1(A_1), .A_2(A_2), .A_3(A_3), .A_4(A_4), .C(pop), .Q_0(minus1_or_0_1_q_0),
    .Q_1(minus1_or_0_1_q_1), .Q_2(minus1_or_0_1_q_2), .Q_3(minus1_or_0_1_q_3), .Q_4(minus1_or_0_1_q_4));
  not not_3 (not_3_out, get_0);
  not not_4 (not_4_out, get_1);
  not not_5 (not_5_out, get_2);
  not not_6 (not_6_out, get_1);
  not not_7 (not_7_out, get_0);
  not not_8 (not_8_out, get_1);
  not not_9 (not_9_out, get_2);
  not not_10 (not_10_out, get_0);
  not not_11 (not_11_out, get_2);
  and get0 (get0_out, not_3_out, not_4_out, not_5_out, get);
  and get5 (get5_out, get_0, not_6_out, get_2, get);
  and get1 (get1_out, not_7_out, not_8_out, get_2, get);
  and get6 (get6_out, get_0, get_1, not_9_out, get);
  and get2 (get2_out, not_10_out, get_1, not_11_out, get);
  and get7 (get7_out, get, get_0, get_1, get_2);
  not not_12 (not_12_out, get_0);
  and get3 (get3_out, not_12_out, get_2, get_1, get);
  or or_2 (or_2_out, get0_out, get5_out);
  or or_3 (or_3_out, get1_out, get6_out);
  or or_4 (or_4_out, get2_out, get7_out);
  Minus1_or_0 minus1_or_0_2 (
    .A_0(A_0), .A_1(A_1), .A_2(A_2), .A_3(A_3), .A_4(A_4), .C(or_2_out), .Q_0(minus1_or_0_2_q_0),
    .Q_1(minus1_or_0_2_q_1), .Q_2(minus1_or_0_2_q_2), .Q_3(minus1_or_0_2_q_3), .Q_4(minus1_or_0_2_q_4));
  Minus2_or_0 minus2_or_0_1 (
    .A_0(A_0), .A_1(A_1), .A_2(A_2), .A_3(A_3), .A_4(A_4), .get(or_3_out), .Q_0(minus2_or_0_1_q_0),
    .Q_1(minus2_or_0_1_q_1), .Q_2(minus2_or_0_1_q_2), .Q_3(minus2_or_0_1_q_3), .Q_4(minus2_or_0_1_q_4));
  Minus3_or_0 minus3_or_0_1 (
    .A_0(A_0), .A_1(A_1), .A_2(A_2), .A_3(A_3), .A_4(A_4), .get(or_4_out), .Q_0(minus3_or_0_1_q_0),
    .Q_1(minus3_or_0_1_q_1), .Q_2(minus3_or_0_1_q_2), .Q_3(minus3_or_0_1_q_3), .Q_4(minus3_or_0_1_q_4));
  Minus4_or_0 minus4_or_0_1 (
    .A_0(A_0), .A_1(A_1), .A_2(A_2), .A_3(A_3), .A_4(A_4), .get(get3_out), .Q_0(minus4_or_0_1_q_0),
    .Q_1(minus4_or_0_1_q_1), .Q_2(minus4_or_0_1_q_2), .Q_3(minus4_or_0_1_q_3), .Q_4(minus4_or_0_1_q_4));
  or q0 (Q_0, minus1_or_0_1_q_0, and_2_out, minus1_or_0_2_q_0, minus2_or_0_1_q_0, minus3_or_0_1_q_0, minus4_or_0_1_q_0);
  or q1 (Q_1, minus1_or_0_1_q_1, and_3_out, minus1_or_0_2_q_1, minus2_or_0_1_q_1, minus3_or_0_1_q_1, minus4_or_0_1_q_1);
  or q2 (Q_2, minus1_or_0_1_q_2, and_4_out, minus2_or_0_1_q_2, minus1_or_0_2_q_2, minus3_or_0_1_q_2, minus4_or_0_1_q_2);
  or q3 (Q_3, minus1_or_0_1_q_3, minus1_or_0_2_q_3, and_5_out, minus2_or_0_1_q_3, minus3_or_0_1_q_3, minus4_or_0_1_q_3);
  or q4 (Q_4, minus1_or_0_1_q_4, minus1_or_0_2_q_4, minus2_or_0_1_q_4, minus3_or_0_1_q_4, and_6_out, minus4_or_0_1_q_4);
endmodule

module in_out (
  input  A,
  input  B,
  output Q
);

  wire not_1_out, not_2_out;

  not not_1 (not_1_out, A);
  not not_2 (not_2_out, B);
  Transistor transistor_1 (.in(A), .out(Q), .gate(not_2_out));
  Transistor #(.\type ("n")) transistor_2 (.in(not_1_out), .out(Q), .gate(not_2_out));
endmodule

module in_out_4 (
  input  Read,
  input  [3:0] IDATA,
  output [3:0] ODATA
);

  in_out in_out_1 (.A(Read), .B(IDATA[3]), .Q(ODATA[3]));
  in_out in_out_2 (.A(Read), .B(IDATA[2]), .Q(ODATA[2]));
  in_out in_out_3 (.A(Read), .B(IDATA[1]), .Q(ODATA[1]));
  in_out in_out_4 (.A(Read), .B(IDATA[0]), .Q(ODATA[0]));
endmodule

module Minus1_or_0 (
  input  A_0,
  input  A_1,
  input  A_2,
  input  A_3,
  input  A_4,
  input  C,
  output Q_0,
  output Q_1,
  output Q_2,
  output Q_3,
  output Q_4
);

  and and_1 (Q_0, C, A_1);
  and and_2 (Q_1, C, A_2);
  and and_3 (Q_2, C, A_3);
  and and_4 (Q_3, C, A_4);
  and and_5 (Q_4, C, A_0);
endmodule

module Minus2_or_0 (
  input  A_0,
  input  A_1,
  input  A_2,
  input  A_3,
  input  A_4,
  input  get,
  output Q_0,
  output Q_1,
  output Q_2,
  output Q_3,
  output Q_4
);

  wire minus1_or_0_1_q_0, minus1_or_0_1_q_1, minus1_or_0_1_q_2, minus1_or_0_1_q_3, minus1_or_0_1_q_4;

  Minus1_or_0 minus1_or_0_1 (
    .A_0(A_0), .A_1(A_1), .A_2(A_2), .A_3(A_3), .A_4(A_4), .C(get), .Q_0(minus1_or_0_1_q_0),
    .Q_1(minus1_or_0_1_q_1), .Q_2(minus1_or_0_1_q_2), .Q_3(minus1_or_0_1_q_3), .Q_4(minus1_or_0_1_q_4));
  Minus1_or_0 minus1_or_0_2 (
    .A_0(minus1_or_0_1_q_0), .A_1(minus1_or_0_1_q_1), .A_2(minus1_or_0_1_q_2), .A_3(minus1_or_0_1_q_3),
    .A_4(minus1_or_0_1_q_4), .C(get), .Q_0(Q_0), .Q_1(Q_1), .Q_2(Q_2), .Q_3(Q_3), .Q_4(Q_4));
endmodule

module Minus3_or_0 (
  input  A_0,
  input  A_1,
  input  A_2,
  input  A_3,
  input  A_4,
  input  get,
  output Q_0,
  output Q_1,
  output Q_2,
  output Q_3,
  output Q_4
);

  wire minus2_or_0_1_q_0, minus2_or_0_1_q_1, minus2_or_0_1_q_2, minus2_or_0_1_q_3, minus2_or_0_1_q_4;

  Minus2_or_0 minus2_or_0_1 (
    .A_0(A_0), .A_1(A_1), .A_2(A_2), .A_3(A_3), .A_4(A_4), .get(get), .Q_0(minus2_or_0_1_q_0),
    .Q_1(minus2_or_0_1_q_1), .Q_2(minus2_or_0_1_q_2), .Q_3(minus2_or_0_1_q_3), .Q_4(minus2_or_0_1_q_4));
  Minus1_or_0 minus1_or_0_1 (
    .A_0(minus2_or_0_1_q_0), .A_1(minus2_or_0_1_q_1), .A_2(minus2_or_0_1_q_2), .A_3(minus2_or_0_1_q_3),
    .A_4(minus2_or_0_1_q_4), .C(get), .Q_0(Q_0), .Q_1(Q_1), .Q_2(Q_2), .Q_3(Q_3), .Q_4(Q_4));
endmodule

module Minus4_or_0 (
  input  A_0,
  input  A_1,
  input  A_2,
  input  A_3,
  input  A_4,
  input  get,
  output Q_0,
  output Q_1,
  output Q_2,
  output Q_3,
  output Q_4
);

  wire minus3_or_0_1_q_0, minus3_or_0_1_q_1, minus3_or_0_1_q_2, minus3_or_0_1_q_3, minus3_or_0_1_q_4;

  Minus3_or_0 minus3_or_0_1 (
    .A_0(A_0), .A_1(A_1), .A_2(A_2), .A_3(A_3), .A_4(A_4), .get(get), .Q_0(minus3_or_0_1_q_0),
    .Q_1(minus3_or_0_1_q_1), .Q_2(minus3_or_0_1_q_2), .Q_3(minus3_or_0_1_q_3), .Q_4(minus3_or_0_1_q_4));
  Minus1_or_0 minus1_or_0_1 (
    .A_0(minus3_or_0_1_q_0), .A_1(minus3_or_0_1_q_1), .A_2(minus3_or_0_1_q_2), .A_3(minus3_or_0_1_q_3),
    .A_4(minus3_or_0_1_q_4), .C(get), .Q_0(Q_0), .Q_1(Q_1), .Q_2(Q_2), .Q_3(Q_3), .Q_4(Q_4));
endmodule
